// Logisim project NEWPROJ.circ as structural Verilog: 5 circuits, main circuit main
// 7-Seg
module main (
  input  Clock,
  input  S0,
  input  S1,
  input  S2,
  input  S3,
  output g,
  output f,
  output a,
  output b,
  output e,
  output d,
  output c
);

  wire bcd_to_7seg_1_a, bcd_to_7seg_1_b, bcd_to_7seg_1_c, bcd_to_7seg_1_d, bcd_to_7seg_1_e, bcd_to_7seg_1_f,
       bcd_to_7seg_1_g;

  BCD_to_7Seg bcd_to_7seg_1 (
    .I3(S3), .I2(S2), .I1(S1), .I0(S0), .a(bcd_to_7seg_1_a), .b(bcd_to_7seg_1_b), .c(bcd_to_7seg_1_c),
    .d(bcd_to_7seg_1_d), .e(bcd_to_7seg_1_e), .f(bcd_to_7seg_1_f), .g(bcd_to_7seg_1_g));
  D_Flip_Flop d_ff_1 (.clk(Clock), .D(bcd_to_7seg_1_a), .Q(a));  // open: Qn, preset, en, reset
  D_Flip_Flop d_ff_2 (.clk(Clock), .D(bcd_to_7seg_1_b), .Q(b));  // open: Qn, preset, en, reset
  D_Flip_Flop d_ff_3 (.clk(Clock), .D(bcd_to_7seg_1_c), .Q(c));  // open: Qn, preset, en, reset
  D_Flip_Flop d_ff_4 (.clk(Clock), .D(bcd_to_7seg_1_d), .Q(d));  // open: Qn, preset, en, reset
  D_Flip_Flop d_ff_5 (.clk(Clock), .D(bcd_to_7seg_1_e), .Q(e));  // open: Qn, preset, en, reset
  D_Flip_Flop d_ff_6 (.clk(Clock), .D(bcd_to_7seg_1_f), .Q(f));  // open: Qn, preset, en, reset
  D_Flip_Flop d_ff_7 (.clk(Clock), .D(bcd_to_7seg_1_g), .Q(g));  // open: Qn, preset, en, reset
endmodule

module BCD_to_7Seg (
  input  I3,
  input  I2,
  input  I1,
  input  I0,
  output a,
  output b,
  output c,
  output d,
  output e,
  output f,
  output g
);

  wire and_1_out, and_2_out, and_3_out, and_4_out, and_5_out, and_6_out, and_7_out, and_8_out, and_9_out,
       and_10_out, and_11_out, and_12_out, and_13_out, and_14_out, and_15_out, and_16_out, not_1_out,
       not_2_out, not_3_out, not_4_out;

  not not_1 (not_1_out, I2);
  and and_1 (and_1_out, not_1_out, not_2_out);
  not not_2 (not_2_out, I0);
  and and_2 (and_2_out, I2, I0);
  not not_3 (not_3_out, I1);
  and and_3 (and_3_out, not_3_out, not_4_out);
  not not_4 (not_4_out, I0);
  and and_4 (and_4_out, I1, I0);
  and and_5 (and_5_out, not_1_out, not_4_out);
  and and_6 (and_6_out, not_4_out, I1);
  and and_7 (and_7_out, not_3_out, I2, I0);
  and and_8 (and_8_out, not_1_out, I1);
  and and_9 (and_9_out, not_1_out, not_4_out);
  and and_10 (and_10_out, not_4_out, I1);
  and and_11 (and_11_out, not_4_out, not_3_out);
  and and_12 (and_12_out, not_3_out, I2);
  and and_13 (and_13_out, I2, not_4_out);
  and and_14 (and_14_out, I2, not_3_out);
  and and_15 (and_15_out, not_1_out, I1);
  and and_16 (and_16_out, I1, not_4_out);
  or or_1 (a, and_1_out, I3, I1, and_2_out);
  or or_2 (b, and_3_out, not_1_out, and_4_out);
  or or_3 (c, I2, not_3_out, I0);
  or or_4 (d, and_5_out, and_6_out, and_7_out, I3, and_8_out);
  or or_5 (e, and_9_out, and_10_out);
  or or_6 (f, and_11_out, and_12_out, and_13_out, I3);
  or or_7 (g, and_14_out, I3, and_15_out, and_16_out);

  // Notes on the sheet:
  //   a
endmodule

module Encoder (
  input  I0,
  input  I1,
  input  I2,
  input  I3,
  input  I4,
  input  I5,
  input  I6,
  input  I7,
  input  I8,
  input  I9,
  output s3,
  output s2,
  output s1,
  output s0
);

  wire and_1_out, and_2_out, and_3_out, and_4_out, and_5_out, and_6_out, and_7_out, and_8_out, and_9_out,
       and_10_out, and_11_out, and_12_out, not_1_out, not_2_out, not_3_out, not_4_out, not_5_out, not_6_out,
       not_7_out;

  not not_1 (not_1_out, I3);
  not not_2 (not_2_out, I4);
  not not_3 (not_3_out, I5);
  not not_4 (not_4_out, I6);
  not not_5 (not_5_out, I7);
  not not_6 (not_6_out, I8);
  not not_7 (not_7_out, I9);
  or or_1 (s3, I8, I9);
  or or_2 (s0, I3, I5, I1, I9, I7);
  and and_1 (and_1_out, I2, not_1_out);
  and and_2 (and_2_out, I3, not_2_out);
  and and_3 (and_3_out, I3, not_3_out);
  and and_4 (and_4_out, I3, not_4_out);
  and and_5 (and_5_out, I6, not_5_out);
  and and_6 (and_6_out, I7, not_6_out);
  and and_7 (and_7_out, I7, not_7_out);
  and and_8 (and_8_out, I4, not_3_out);
  and and_9 (and_9_out, I5, not_4_out);
  and and_10 (and_10_out, I6, not_5_out);
  and and_11 (and_11_out, I7, not_6_out);
  and and_12 (and_12_out, I7, not_7_out);
  or or_3 (s1, and_1_out, and_2_out, and_3_out, and_4_out, and_5_out, and_6_out, and_7_out);
  or or_4 (s2, and_8_out, and_9_out, and_10_out, and_11_out, and_12_out);
endmodule

module keypad (
  input  _1,
  input  _2,
  input  _3,
  input  _4,
  input  _5,
  input  _6,
  input  _7,
  input  _8,
  input  _9,
  input  _0,
  input  Enter
);

  wire encoder_1_s0, encoder_1_s1, encoder_1_s2, encoder_1_s3, flip_1_a_2, flip_1_b_2, flip_1_c_2,
       flip_1_d_2, flip_1_e_2, flip_1_f_2, flip_1_g_2, main_1_a, main_1_b, main_1_c, main_1_d, main_1_e,
       main_1_f, main_1_g;

  main main_1 (
    .Clock(Enter), .S0(encoder_1_s0), .S1(encoder_1_s1), .S2(encoder_1_s2), .S3(encoder_1_s3), .e(main_1_e),
    .d(main_1_d), .c(main_1_c), .g(main_1_g), .f(main_1_f), .a(main_1_a), .b(main_1_b));
  _7_Segment_Display u_7_segment_display_1 (
    .g(main_1_g), .f(main_1_f), .a(main_1_a), .b(main_1_b), .e(main_1_e), .d(main_1_d), .c(main_1_c));  // open: dp
  _7_Segment_Display u_7_segment_display_2 (
    .g(flip_1_g_2), .f(flip_1_f_2), .a(flip_1_a_2), .b(flip_1_b_2), .e(flip_1_e_2), .d(flip_1_d_2),
    .c(flip_1_c_2));  // open: dp
  flip flip_1 (
    .Clock(Enter), .a(main_1_a), .b(main_1_b), .c(main_1_c), .d(main_1_d), .e(main_1_e), .f(main_1_f),
    .g(main_1_g), .e_2(flip_1_e_2), .d_2(flip_1_d_2), .c_2(flip_1_c_2), .g_2(flip_1_g_2), .f_2(flip_1_f_2),
    .a_2(flip_1_a_2), .b_2(flip_1_b_2));
  Encoder encoder_1 (
    .I0(_0), .I1(_1), .I2(_2), .I3(_3), .I4(_4), .I5(_5), .I6(_6), .I7(_7), .I8(_8), .I9(_9),
    .s3(encoder_1_s3), .s2(encoder_1_s2), .s1(encoder_1_s1), .s0(encoder_1_s0));
endmodule

// FLIP-FLOP
module flip (
  input  Clock,
  input  a,
  input  b,
  input  c,
  input  d,
  input  e,
  input  f,
  input  g,
  output g_2,
  output f_2,
  output a_2,
  output b_2,
  output e_2,
  output d_2,
  output c_2
);

  D_Flip_Flop d_ff_1 (.clk(Clock), .D(a), .Q(a_2));  // open: Qn, preset, en, reset
  D_Flip_Flop d_ff_2 (.clk(Clock), .D(b), .Q(b_2));  // open: Qn, preset, en, reset
  D_Flip_Flop d_ff_3 (.clk(Clock), .D(c), .Q(c_2));  // open: Qn, preset, en, reset
  D_Flip_Flop d_ff_4 (.clk(Clock), .D(d), .Q(d_2));  // open: Qn, preset, en, reset
  D_Flip_Flop d_ff_5 (.clk(Clock), .D(e), .Q(e_2));  // open: Qn, preset, en, reset
  D_Flip_Flop d_ff_6 (.clk(Clock), .D(f), .Q(f_2));  // open: Qn, preset, en, reset
  D_Flip_Flop d_ff_7 (.clk(Clock), .D(g), .Q(g_2));  // open: Qn, preset, en, reset
endmodule
